// Digital circuit UTS_1_13.dig as structural Verilog
module UTS_1_13 (
  input  x,
  input  y,
  input  z
);

  wire and_1_out, and_2_out, and_3_out, not_1_out, not_2_out, not_3_out, or_1_out;

  not not_1 (not_1_out, z);
  not not_2 (not_2_out, x);
  not not_3 (not_3_out, y);
  and and_1 (and_1_out, not_2_out, y, z);
  and and_2 (and_2_out, x, not_3_out);
  and and_3 (and_3_out, y, not_1_out);
  or or_1 (or_1_out, and_1_out, and_2_out, and_3_out);
  LED A (.in(or_1_out));

  // Notes on the sheet:
  //   Ida Farida  213050024
  //   13. x'yz + xy' + yz'
endmodule
