// Digital circuit UTS_1_15.dig as structural Verilog
module UTS_1_15 (
  input  a,
  input  b,
  input  c,
  input  d
);

  wire and_1_out, and_2_out, and_3_out, and_4_out, not_1_out, not_2_out, not_3_out, not_4_out, not_5_out,
       not_6_out, or_1_out;

  not not_1 (not_1_out, c);
  not not_2 (not_2_out, d);
  not not_3 (not_3_out, b);
  not not_4 (not_4_out, c);
  not not_5 (not_5_out, a);
  not not_6 (not_6_out, d);
  and and_1 (and_1_out, a, b, not_1_out);
  and and_2 (and_2_out, not_4_out, d);
  and and_3 (and_3_out, not_5_out, c, not_2_out);
  and and_4 (and_4_out, not_3_out, c, not_6_out);
  or or_1 (or_1_out, and_1_out, and_2_out, and_3_out, and_4_out);
  LED x (.in(or_1_out));

  // Notes on the sheet:
  //   Ida Farida  213050024
  //   abc' + c'd + a'cd' + b'cd'
endmodule
