// Digital circuit UTS_1_4.dig as structural Verilog
module UTS_1_4 (
  input  A,
  input  B,
  input  C,
  input  D,
  output X
);

  wire and_1_out, and_2_out, and_3_out, not_1_out, not_2_out, not_3_out, not_4_out;

  not not_1 (not_1_out, B);
  not not_2 (not_2_out, A);
  not not_3 (not_3_out, A);
  not not_4 (not_4_out, C);
  and and_1 (and_1_out, not_2_out, B);
  and and_2 (and_2_out, not_3_out, not_1_out, not_4_out);
  and and_3 (and_3_out, C, D);
  or or_1 (X, and_1_out, and_2_out, and_3_out);

  // Notes on the sheet:
  //   IDA FARIDA   213050024
  //   A'B + A'B'C' + CD
endmodule
