// Digital circuit UTS_1_6.dig as structural Verilog
module UTS_1_6 (
  input  A,
  input  B,
  input  C,
  input  D,
  output X
);

  wire and_1_out, and_2_out, and_3_out, and_4_out, not_1_out, not_2_out, not_3_out, not_4_out, not_5_out;

  not not_1 (not_1_out, B);
  not not_2 (not_2_out, C);
  not not_3 (not_3_out, A);
  not not_4 (not_4_out, A);
  not not_5 (not_5_out, A);
  and and_1 (and_1_out, not_3_out, not_1_out, C);
  and and_2 (and_2_out, not_4_out, not_2_out, D);
  and and_3 (and_3_out, not_5_out, B, C);
  and and_4 (and_4_out, A, B, D);
  or or_1 (X, and_1_out, and_2_out, and_3_out, and_4_out);

  // Notes on the sheet:
  //   IDA FARIDA  213050024
  //   A'B'C + A'C'D + A'BC +ABD
endmodule
