// Digital circuit UTS_1_8.dig as structural Verilog
module UTS_1_8 (
  input  A,
  input  B,
  input  C,
  input  D
);

  wire and_1_out, and_2_out, and_3_out, and_4_out, and_5_out, not_1_out, not_2_out, not_3_out, or_1_out;

  not not_1 (not_1_out, D);
  not not_2 (not_2_out, A);
  not not_3 (not_3_out, C);
  and and_1 (and_1_out, not_2_out, B, not_1_out);
  and and_2 (and_2_out, B, C, D);
  and and_3 (and_3_out, A, B, not_3_out);
  and and_4 (and_4_out, B, D);
  and and_5 (and_5_out, A, B, B);
  or or_1 (or_1_out, and_1_out, and_2_out, and_3_out, and_4_out, and_5_out);
  LED Y (.in(or_1_out));

  // Notes on the sheet:
  //   A'BD' + BDC + ABC' + BD + ABC
  //   IDA FARIDA   213050024
endmodule
