// Digital circuit UTS_1_9.dig as structural Verilog
module UTS_1_9 (
  input  A,
  input  B,
  input  C,
  input  D
);

  wire and_1_out, and_2_out, and_3_out, and_4_out, and_5_out, not_1_out, not_2_out, not_3_out, not_4_out,
       not_5_out, not_6_out, not_7_out, not_8_out, or_1_out;

  not not_1 (not_1_out, D);
  not not_2 (not_2_out, B);
  not not_3 (not_3_out, C);
  not not_4 (not_4_out, C);
  not not_5 (not_5_out, C);
  not not_6 (not_6_out, D);
  not not_7 (not_7_out, A);
  not not_8 (not_8_out, C);
  and and_1 (and_1_out, A, not_2_out, not_3_out);
  and and_2 (and_2_out, A, not_4_out, not_6_out);
  and and_3 (and_3_out, A, B, D);
  and and_4 (and_4_out, B, not_5_out, D);
  and and_5 (and_5_out, not_7_out, B, not_8_out, not_1_out);
  or or_1 (or_1_out, and_1_out, and_2_out, and_3_out, and_4_out, and_5_out);
  LED X (.in(or_1_out));

  // Notes on the sheet:
  //   AB'C' +  AC'D' + ABD + BC'D + A'BC'D'
  //   IDA FARIDA   213050024
endmodule
